// Logisim project Marcos_Arquitetura.circ as structural Verilog: 5 circuits, main circuit main
module main (
  input  [3:0] A,
  input  [3:0] B,
  output Overflow,
  output out_4,
  output [3:0] S,
  output [3:0] S_2
);

  // Probe on A
  // Probe on S
  // Probe on B
  // Probe on A
  ADD_4 add_4_1 (.A(A), .Overflow(Overflow), .B(B), .out_4(S));
  // Probe on B
  SUB_4 sub_4_1 (.A(A), .Overflow(out_4), .B(B), .out_4(S_2));
  // Probe on S_2
endmodule

module ADD_1 (
  input  A,
  input  B,
  input  C,
  output SOMA,
  output VAI_1
);

  wire and_1_out, and_2_out, or_1_out, xor_1_out;

  xor xor_1 (xor_1_out, C, B);
  or or_1 (or_1_out, B, C);
  and and_1 (and_1_out, B, C);
  xor xor_2 (SOMA, xor_1_out, A);
  and and_2 (and_2_out, or_1_out, A);
  or or_2 (VAI_1, and_2_out, and_1_out);
endmodule

module ADD_4 (
  input  [3:0] B,
  input  [3:0] A,
  output Overflow,
  output [3:0] out_4
);

  wire add_1_2_vai_1, add_1_3_vai_1, add_1_4_vai_1;

  // Probe on A
  ADD_1 add_1_1 (.VAI_1(Overflow), .A(A[3]), .B(B[3]), .C(add_1_2_vai_1), .SOMA(out_4[3]));
  ADD_1 add_1_2 (.VAI_1(add_1_2_vai_1), .A(A[2]), .B(B[2]), .C(add_1_3_vai_1), .SOMA(out_4[2]));
  ADD_1 add_1_3 (.VAI_1(add_1_3_vai_1), .A(A[1]), .B(B[1]), .C(add_1_4_vai_1), .SOMA(out_4[1]));
  // Probe on out_4
  ADD_1 add_1_4 (.VAI_1(add_1_4_vai_1), .A(A[0]), .B(B[0]), .C(1'b0), .SOMA(out_4[0]));
  // Probe on B
endmodule

module SUB_1 (
  input  A,
  input  B,
  input  C,
  output SOMA,
  output VAI_1
);

  wire and_1_out, and_2_out, or_1_out, xor_1_out;

  xor xor_1 (xor_1_out, C, B);
  or or_1 (or_1_out, B, C);
  and and_1 (and_1_out, B, C);
  xor xor_2 (SOMA, xor_1_out, A);
  and and_2 (and_2_out, or_1_out, ~A);  // AND_Gate
  or or_2 (VAI_1, and_2_out, and_1_out);
endmodule

module SUB_4 (
  input  [3:0] B,
  input  [3:0] A,
  output Overflow,
  output [3:0] out_4
);

  wire sub_1_2_vai_1, sub_1_3_vai_1, sub_1_4_vai_1;

  // Probe on A
  SUB_1 sub_1_1 (.VAI_1(Overflow), .A(A[3]), .B(B[3]), .C(sub_1_2_vai_1), .SOMA(out_4[3]));
  SUB_1 sub_1_2 (.VAI_1(sub_1_2_vai_1), .A(A[2]), .B(B[2]), .C(sub_1_3_vai_1), .SOMA(out_4[2]));
  SUB_1 sub_1_3 (.VAI_1(sub_1_3_vai_1), .A(A[1]), .B(B[1]), .C(sub_1_4_vai_1), .SOMA(out_4[1]));
  // Probe on out_4
  // Probe on B
  SUB_1 sub_1_4 (.VAI_1(sub_1_4_vai_1), .A(A[0]), .B(B[0]), .C(1'b0), .SOMA(out_4[0]));
endmodule
